// Logisim project s-mips.circ as structural Verilog
module S_MIPS_Board (
  input  DESHABILITAR_DISPATCHER,
  output halt
);

  wire button_1_out, CLK, CS, d_ff_1_q, LCLR, LoadRAM, LoadRAMOn, LW, R_R_W, R_W, ram_dispatcher_1_finished,
       RCS, Reset_out, RST, TTY_EN;
  wire [2:0] KDB;
  wire [3:0] LMask, Mask, ram_1_read_time, ram_1_write_time, RMask;
  wire [6:0] KDB_DATA, TTY_DATA;
  wire [15:0] Addr, LAddr, RAddr;
  wire [31:0] I0, I1, I2, I3, LData, ram_1_data_out_0, ram_1_data_out_1, ram_1_data_out_2, ram_1_data_out_3,
       RI0, RI1, RI2, RI3;

  TTY #(.rows(25), .cols(80)) tty_1 (.data(TTY_DATA), .clk(CLK), .we(TTY_EN), .clr(RST));
  not not_1 (LoadRAMOn, ram_dispatcher_1_finished);
  RAM_Dispatcher ram_dispatcher_1 (
    .WriteTime(ram_1_write_time), .Clock(CLK), .Data(LData), .Address(LAddr), .Mask(LMask),
    .Finished(ram_dispatcher_1_finished), .Write(LW), .CLR(LCLR));
  Keyboard #(.buflen(64)) keyboard_1 (.clk(CLK), .re(KDB[0]), .avail(KDB[2]), .data(KDB_DATA));  // open: clr
  RAM ram_1 (
    .Address(RAddr), .Data_Out_0(ram_1_data_out_0), .Data_Out_1(ram_1_data_out_1),
    .Data_Out_2(ram_1_data_out_2), .Data_Out_3(ram_1_data_out_3), .Data_In_0(RI0), .Data_In_1(RI1),
    .Data_In_2(RI2), .Data_In_3(RI3), .Mask(RMask), .nRead_Write(R_R_W), .Chip_Select(RCS),
    .Read_Time(ram_1_read_time), .Reset(button_1_out), .Write_Time(ram_1_write_time));
  Button button_1 (.out(button_1_out));
  D_Flip_Flop d_ff_1 (.clk(CLK), .D(1'b1), .Q(d_ff_1_q), .reset(Reset_out));  // open: Qn, preset, en
  Button Reset (.out(Reset_out));
  S_MIPS s_mips_1 (
    .Kbd_Enable(KDB[0]), .Address(Addr), .Kbd_Clear(KDB[1]), .Kbd_Available(KDB[2]), .RAM_In_0(I0),
    .Kbd_ASCII_Data(KDB_DATA), .RAM_In_1(I1), .TTY_Enable(TTY_EN), .RAM_In_2(I2), .RAM_In_3(I3),
    .TTY_ASCII_Data(TTY_DATA), .Reset(RST), .RAM_Out_0(ram_1_data_out_0), .Clock(CLK),
    .RAM_Out_1(ram_1_data_out_1), .Stop(halt), .RAM_Out_2(ram_1_data_out_2), .RAM_Out_3(ram_1_data_out_3),
    .Mask(Mask), .Read_Time(ram_1_read_time), .Write_Time(ram_1_write_time), .nRead_Write(R_W),
    .Chip_Select(CS));
  D_Flip_Flop d_ff_2 (.clk(CLK), .D(d_ff_1_q), .Qn(LCLR), .reset(Reset_out));  // open: Q, preset, en
  or or_1 (RST, LCLR, LoadRAM);
  Clock clock_1 (.out(CLK));
  Multiplexer #(.width(32), .enable("false")) multiplexer_1 (.in0(I0), .in1(LData), .out(RI0), .sel(LoadRAM));
  Multiplexer #(.width(32), .enable("false")) multiplexer_2 (.in0(I1), .in1(LData), .out(RI1), .sel(LoadRAM));
  Multiplexer #(.width(32), .enable("false")) multiplexer_3 (.in0(I2), .in1(LData), .out(RI2), .sel(LoadRAM));
  Multiplexer #(.width(32), .enable("false")) multiplexer_4 (.in0(I3), .in1(LData), .out(RI3), .sel(LoadRAM));
  and and_1 (LoadRAM, ~DESHABILITAR_DISPATCHER, LoadRAMOn);  // AND_Gate
  Multiplexer #(.width(16), .enable("false")) multiplexer_5 (.in0(Addr), .in1(LAddr), .out(RAddr), .sel(LoadRAM));
  Multiplexer #(.width(4), .enable("false")) multiplexer_6 (.in0(Mask), .in1(LMask), .out(RMask), .sel(LoadRAM));
  Multiplexer #(.enable("false")) multiplexer_7 (.in0(CS), .in1(LW), .out(RCS), .sel(LoadRAM));
  Multiplexer #(.enable("false")) multiplexer_8 (.in0(R_W), .in1(LW), .out(R_R_W), .sel(LoadRAM));

  // Notes on the sheet:
  //   NO MODIFICAR
  //   Keyboard
endmodule

module RAM (
  input  [15:0] Address,
  input  [31:0] Data_In_0,
  input  [31:0] Data_In_1,
  input  [31:0] Data_In_2,
  input  [31:0] Data_In_3,
  input  [3:0] Mask,
  input  nRead_Write,
  input  Chip_Select,
  input  Reset,
  output [31:0] Data_Out_0,
  output [31:0] Data_Out_1,
  output [31:0] Data_Out_2,
  output [31:0] Data_Out_3,
  output [3:0] Read_Time,
  output [3:0] Write_Time
);

  wire and_2_out, and_3_out, and_4_out, and_5_out, and_6_out, and_7_out, and_8_out, and_9_out, Changed, CLK,
       comparator_2_eq, comparator_3_eq, comparator_4_eq, comparator_5_eq, comparator_6_eq, Count,
       demultiplexer_3_out0, Idle, Idle_q, Load, Load0, Load1, nand_1_out, or_1_out, or_2_out, or_3_out,
       or_4_out, or_5_out, or_6_out, or_7_out, or_8_out, or_9_out, or_10_out, Proc_q, Update_Mem, Zero_Time;
  wire [3:0] counter_1_q, multiplexer_1_out, subtractor_1_out;
  wire [31:0] register_1_q, register_2_q, register_3_q, register_4_q, register_5_q;

  // Probe on 4'b0011
  // Probe on 4'b0010
  Multiplexer #(.width(4), .enable("false")) multiplexer_1 (
    .in0(4'b0011), .in1(4'b0010), .out(multiplexer_1_out), .sel(nRead_Write));
  or or_1 (or_1_out, Idle, Update_Mem);
  or or_2 (or_2_out, ~Chip_Select, Reset);  // OR_Gate
  Subtractor #(.width(4)) subtractor_1 (.a(multiplexer_1_out), .b(4'b0010), .out(subtractor_1_out));  // open: bin, bout
  Demultiplexer #(.enable("false")) demultiplexer_1 (.out0(Idle), .out1(Load0), .in(Idle_q), .sel(Changed));
  D_Flip_Flop u_Idle (.clk(CLK), .D(or_1_out), .Q(Idle_q), .preset(or_2_out));  // open: Qn, en, reset
  // Probe on counter_1_q
  Counter #(.width(4), .max('hf)) counter_1 (
    .load(Load), .D(subtractor_1_out), .count(Count), .Q(counter_1_q), .clk(CLK), .clr(or_3_out));  // open: carry
  or or_3 (or_3_out, ~Chip_Select, Reset);  // OR_Gate
  Comparator #(.width(4), .mode("unsigned")) comparator_1 (
    .a(4'b0000), .b(counter_1_q), .eq(Zero_Time));  // open: gt, lt
  or or_4 (or_4_out, Count, Load0, Load1);
  Register #(.width(32)) register_1 (.D(Data_In_0), .en(Chip_Select), .Q(register_1_q), .clk(CLK), .clr(or_5_out));
  or or_5 (or_5_out, ~Chip_Select, Reset);  // OR_Gate
  Register #(.width(32)) register_2 (.D(Data_In_1), .en(Chip_Select), .Q(register_2_q), .clk(CLK), .clr(or_6_out));
  or or_6 (or_6_out, ~Chip_Select, Reset);  // OR_Gate
  Register #(.width(32)) register_3 (.D(Data_In_2), .en(Chip_Select), .Q(register_3_q), .clk(CLK), .clr(or_7_out));
  or or_7 (or_7_out, ~Chip_Select, Reset);  // OR_Gate
  Register #(.width(32)) register_4 (.D(Data_In_3), .en(Chip_Select), .Q(register_4_q), .clk(CLK), .clr(or_8_out));
  or or_8 (or_8_out, ~Chip_Select, Reset);  // OR_Gate
  Register #(.width(32)) register_5 (
    .D({{11{1'b1}}, nRead_Write, Mask, Address}), .en(Chip_Select), .Q(register_5_q), .clk(CLK),
    .clr(or_9_out));
  or or_9 (or_9_out, ~Chip_Select, Reset);  // OR_Gate
  D_Flip_Flop Proc (.clk(CLK), .D(or_4_out), .Q(Proc_q), .reset(or_10_out));  // open: Qn, preset, en
  or or_10 (or_10_out, ~Chip_Select, Reset);  // OR_Gate
  Demultiplexer #(.enable("false")) demultiplexer_2 (
    .out0(Count), .out1(Update_Mem), .in(demultiplexer_3_out0), .sel(Zero_Time));
  Demultiplexer #(.enable("false")) demultiplexer_3 (
    .out0(demultiplexer_3_out0), .out1(Load1), .in(Proc_q), .sel(Changed));
  Clock clock_1 (.out(CLK));
  Comparator #(.width(32)) comparator_2 (.a(register_1_q), .b(Data_In_0), .eq(comparator_2_eq));  // open: gt, lt
  Comparator #(.width(32)) comparator_3 (.a(register_2_q), .b(Data_In_1), .eq(comparator_3_eq));  // open: gt, lt
  Comparator #(.width(32)) comparator_4 (.a(register_3_q), .b(Data_In_2), .eq(comparator_4_eq));  // open: gt, lt
  Comparator #(.width(32)) comparator_5 (.a(register_4_q), .b(Data_In_3), .eq(comparator_5_eq));  // open: gt, lt
  Comparator #(.width(32)) comparator_6 (
    .a(register_5_q), .b({{11{1'b1}}, nRead_Write, Mask, Address}), .eq(comparator_6_eq));  // open: gt, lt
  nand nand_1 (nand_1_out, comparator_6_eq, comparator_2_eq, comparator_3_eq, comparator_4_eq, comparator_5_eq);
  and and_1 (Changed, nand_1_out, Chip_Select);
  or or_11 (Load, Count, Load1, Load0);
  and and_2 (and_2_out, Mask[0], Update_Mem, nRead_Write);
  and and_3 (and_3_out, Mask[1], Update_Mem, nRead_Write);
  and and_4 (and_4_out, Mask[2], Update_Mem, nRead_Write);
  and and_5 (and_5_out, Mask[3], Update_Mem, nRead_Write);
  RAM_part #(.addrWidth(16), .dataWidth(32), .bus("separate")) ram_1 (
    .addr(Address), .din(Data_In_0), .data(Data_Out_0), .str(and_2_out), .sel(Chip_Select), .clk(CLK),
    .ld(and_6_out), .clr(Reset));
  and and_6 (and_6_out, ~nRead_Write, Idle);  // AND_Gate
  RAM_part #(.addrWidth(16), .dataWidth(32), .bus("separate")) ram_2 (
    .addr(Address), .din(Data_In_1), .data(Data_Out_1), .str(and_3_out), .sel(Chip_Select), .clk(CLK),
    .ld(and_7_out), .clr(Reset));
  and and_7 (and_7_out, ~nRead_Write, Idle);  // AND_Gate
  RAM_part #(.addrWidth(16), .dataWidth(32), .bus("separate")) ram_3 (
    .addr(Address), .din(Data_In_2), .data(Data_Out_2), .str(and_4_out), .sel(Chip_Select), .clk(CLK),
    .ld(and_8_out), .clr(Reset));
  and and_8 (and_8_out, ~nRead_Write, Idle);  // AND_Gate
  RAM_part #(.addrWidth(16), .dataWidth(32), .bus("separate")) ram_4 (
    .addr(Address), .din(Data_In_3), .data(Data_Out_3), .str(and_5_out), .sel(Chip_Select), .clk(CLK),
    .ld(and_9_out), .clr(Reset));
  and and_9 (and_9_out, ~nRead_Write, Idle);  // AND_Gate

  assign Read_Time = 4'b0011;
  assign Write_Time = 4'b0010;

  // Other names for the same wires on the sheet: M0 = Mask[0]; M1 = Mask[1]; M2 = Mask[2]; M3 = Mask[3];
  //   RW = nRead_Write; CLR = Reset; CS = Chip_Select; Load2 = Count

  // Notes on the sheet:
  //   NO MODIFICAR
  //   excepto quizás los valores RT y WT
  //   BANK0
  //   BANK1
  //   BANK2
  //   BANK3
endmodule

module S_MIPS (
  input  Kbd_Available,
  input  [6:0] Kbd_ASCII_Data,
  input  [31:0] RAM_Out_0,
  input  [31:0] RAM_Out_1,
  input  Reset,
  input  [31:0] RAM_Out_2,
  input  Clock,
  input  [31:0] RAM_Out_3,
  input  [3:0] Read_Time,
  input  [3:0] Write_Time,
  output Kbd_Enable,
  output [15:0] Address,
  output Kbd_Clear,
  output TTY_Enable,
  output [6:0] TTY_ASCII_Data,
  output Stop,
  output [31:0] RAM_In_0,
  output [31:0] RAM_In_1,
  output [31:0] RAM_In_2,
  output [31:0] RAM_In_3,
  output [3:0] Mask,
  output nRead_Write,
  output Chip_Select
);

  wire control_unit_1_e_inst, control_unit_1_e_pc, control_unit_1_read_end, halt, PC_Address, read_RAM,
       write_RAM;
  wire [31:0] Dir_RAM, value_read, value_write;

  Control_Unit_2 control_unit_1 (
    .Clock(Clock), .Read_RAM(read_RAM), .Reset(Reset), .Write_RAM(write_RAM), .halt(halt),
    .Read_RAM_time(Read_Time), .Write_RAM_time(Write_Time), .E_inst(control_unit_1_e_inst), .CS(Chip_Select),
    .Read_End(control_unit_1_read_end), .R_W(nRead_Write), .E_PC(control_unit_1_e_pc), .End(Stop),
    .PC_Address(PC_Address));
  Data_Path_2 data_path_1 (
    .Clock(Clock), .Instruction(value_read), .Reset(Reset), .E_PC(control_unit_1_e_pc),
    .Read_RAM(control_unit_1_read_end), .Keyboard(Kbd_ASCII_Data), .Dir_Address(Dir_RAM),
    .RAM__w(value_write), .halt(halt), .Read_RAM_2(read_RAM), .kbd(Kbd_Enable), .tty(TTY_Enable),
    .Write_RAM(write_RAM), .tty_DATA(TTY_ASCII_Data), .E_inst(control_unit_1_e_inst),
    .KBD_AVAIL(Kbd_Available), .PC_Address(PC_Address));
  Write_RAM write_ram_1 (
    .Value(value_write), .Bank_0(RAM_In_0), .Bank_2(RAM_In_2), .Bank_1(RAM_In_1), .Bank_3(RAM_In_3),
    .Dir_RAM(Dir_RAM), .ADDR(Address), .Mask(Mask));
  Read_RAM read_ram_1 (
    .Bank_0(RAM_Out_0), .Bank_1(RAM_Out_1), .Bank_2(RAM_Out_2), .Bank_3(RAM_Out_3), .Value(value_read),
    .Dir_RAM(Dir_RAM));

  assign Kbd_Clear = Reset;

  // Other names for the same wires on the sheet: CLK = Clock; CLR = Reset; CS = Chip_Select;
  //   KBD_AVAIL = Kbd_Available; KBD_DATA[6:0] = Kbd_ASCII_Data; RAM_A[15:0] = Address; RAM_INPUT_0[31:0] = RAM_In_0;
  //   RAM_INPUT_1[31:0] = RAM_In_1; RAM_INPUT_2[31:0] = RAM_In_2; RAM_INPUT_3[31:0] = RAM_In_3; RAM_MASK[3:0] = Mask;
  //   RAM_OUTPUT_0[31:0] = RAM_Out_0; RAM_OUTPUT_1[31:0] = RAM_Out_1; RAM_OUTPUT_2[31:0] = RAM_Out_2;
  //   RAM_OUTPUT_3[31:0] = RAM_Out_3; RW = nRead_Write; TTY_DATA[6:0] = TTY_ASCII_Data

  // Notes on the sheet:
  //   RAM ADDRESS
  //   DATA FROM RAM
  //   DATA TO RAM
  //   DATA WRITE MASK
  //   RAM TIMING
  //   RAM CONTROL
  //   KEYBOARD
  //   TTY
  //   SEQUENCING
  //   Main 
  //   Memory Handling
endmodule

module RAM_Dispatcher (
  input  [3:0] WriteTime,
  input  Clock,
  input  CLR,
  output [31:0] Data,
  output [15:0] Address,
  output [3:0] Mask,
  output Finished,
  output Write
);

  wire demultiplexer_2_out1, demultiplexer_3_out1, End, IDLE_q, IncAddr, Load, or_1_out, or_2_out, While_q,
       WriteEnd;
  wire [3:0] counter_1_q;
  wire [31:0] CurrentAddress_q;

  Counter #(.width(32), .max('hffffffff)) CurrentAddress (
    .count(IncAddr), .Q({CurrentAddress_q[31:18], Address, CurrentAddress_q[1:0]}), .clk(Clock), .clr(CLR));  // open: load, D, carry
  or or_1 (or_1_out, IncAddr, demultiplexer_3_out1, Finished);
  D_Flip_Flop IDLE (.clk(Clock), .D(or_1_out), .Q(IDLE_q), .preset(CLR));  // open: Qn, en, reset
  Demultiplexer #(.enable("false")) demultiplexer_1 (.out0(Load), .out1(Finished), .in(IDLE_q), .sel(End));
  D_Flip_Flop While (.clk(Clock), .D(or_2_out), .Q(While_q), .reset(CLR));  // open: Qn, preset, en
  or or_2 (or_2_out, Write, Load);
  RAM_part #(.addrWidth(18), .dataWidth(32)) ram_1 (
    .addr({Address, CurrentAddress_q[1:0]}), .data(Data), .clk(Clock));  // open: sel, ld, clr
  Demultiplexer #(.enable("false")) demultiplexer_2 (
    .out0(Write), .out1(demultiplexer_2_out1), .in(While_q), .sel(WriteEnd));
  Decoder #(.select(2)) decoder_1 (
    .out0(Mask[0]), .out1(Mask[1]), .out2(Mask[2]), .out3(Mask[3]), .sel(CurrentAddress_q[1:0]));  // open: en
  Demultiplexer #(.enable("false")) demultiplexer_3 (
    .out0(IncAddr), .out1(demultiplexer_3_out1), .in(demultiplexer_2_out1), .sel(End));
  Counter #(.width(4), .max('hf)) counter_1 (
    .load(Load), .D(WriteTime), .count(Write), .Q(counter_1_q), .clk(Clock));  // open: carry, clr
  Comparator #(.width(32)) comparator_1 (.a(Data), .b({32{1'b1}}), .eq(End));  // open: gt, lt
  Comparator #(.width(4)) comparator_2 (.a(4'b0000), .b(counter_1_q), .eq(WriteEnd));  // open: gt, lt

  // Other names for the same wires on the sheet: CLK = Clock; Count = Write; WT[3:0] = WriteTime
endmodule

// Control \n Unit
module Control_Unit_2 (
  input  Clock,
  input  Read_RAM,
  input  Reset,
  input  Write_RAM,
  input  [3:0] Read_RAM_time,
  input  halt,
  input  [3:0] Write_RAM_time,
  output E_inst,
  output CS,
  output Read_End,
  output R_W,
  output E_PC,
  output End,
  output PC_Address
);

  wire chip_1, chip_2, crono_rst_1, crono_rst_2, demultiplexer_1_out1, demultiplexer_2_out0,
       demultiplexer_3_out0, demultiplexer_4_out0, demultiplexer_4_out1, demultiplexer_5_out0, IDLE_q,
       Load_Inst_q, or_2_out, or_3_out, or_6_out, or_8_out, RAM, RAM_read_load, timer_1_finish,
       timer_2_finish;
  wire [3:0] multiplexer_1_out;

  or or_1 (E_PC, demultiplexer_3_out0, RAM_read_load);
  or or_2 (or_2_out, demultiplexer_3_out0, RAM_read_load, demultiplexer_1_out1);
  D_Flip_Flop IDLE (.clk(Clock), .D(or_2_out), .Q(IDLE_q), .preset(Reset));  // open: Qn, en, reset
  Demultiplexer #(.enable("false")) demultiplexer_1 (
    .out0(crono_rst_1), .out1(demultiplexer_1_out1), .in(IDLE_q), .sel(Reset));
  or or_3 (or_3_out, demultiplexer_2_out0, crono_rst_1);
  D_Flip_Flop Read_Inst (.clk(Clock), .D(or_3_out), .Q(chip_1), .reset(Reset));  // open: Qn, preset, en
  Demultiplexer #(.enable("false")) demultiplexer_2 (
    .out0(demultiplexer_2_out0), .out1(E_inst), .in(chip_1), .sel(timer_1_finish));
  Timer timer_1 (.Time(Read_RAM_time), .reset(crono_rst_1), .clock(Clock), .finish(timer_1_finish));
  or or_4 (RAM, Read_RAM, Write_RAM);
  D_Flip_Flop Load_Inst (.clk(Clock), .D(E_inst), .Q(Load_Inst_q), .reset(Reset));  // open: Qn, preset, en
  Demultiplexer #(.enable("false")) demultiplexer_3 (
    .out0(demultiplexer_3_out0), .out1(crono_rst_2), .in(demultiplexer_4_out0), .sel(RAM));
  Demultiplexer #(.enable("false")) demultiplexer_4 (
    .out0(demultiplexer_4_out0), .out1(demultiplexer_4_out1), .in(Load_Inst_q), .sel(halt));
  or or_5 (CS, chip_1, chip_2);
  or or_6 (or_6_out, demultiplexer_4_out1, End);
  D_Flip_Flop u_Halt (.clk(Clock), .D(or_6_out), .Q(End), .reset(Reset));  // open: Qn, preset, en
  and and_1 (R_W, Write_RAM, chip_2);
  or or_7 (PC_Address, chip_1, crono_rst_1, E_PC);
  or or_8 (or_8_out, demultiplexer_5_out0, crono_rst_2);
  Multiplexer #(.width(4), .enable("false")) multiplexer_1 (
    .in0(Read_RAM_time), .in1(Write_RAM_time), .out(multiplexer_1_out), .sel(Write_RAM));
  D_Flip_Flop d_ff_1 (.clk(Clock), .D(or_8_out), .Q(chip_2), .reset(Reset));  // open: Qn, preset, en
  Timer timer_2 (.Time(multiplexer_1_out), .reset(crono_rst_2), .clock(Clock), .finish(timer_2_finish));
  Demultiplexer #(.enable("false")) demultiplexer_5 (
    .out0(demultiplexer_5_out0), .out1(Read_End), .in(chip_2), .sel(timer_2_finish));
  D_Flip_Flop Load_Read (.clk(Clock), .D(Read_End), .Q(RAM_read_load), .reset(Reset));  // open: Qn, preset, en

  // Other names for the same wires on the sheet: clk = Clock; R_W_RAM = R_W; Read_time[3:0] = Read_RAM_time;
  //   rst = Reset; Write_time[3:0] = Write_RAM_time

  // Notes on the sheet:
  //   Input Area
  //   State Signals
  //   ASM
  //   Control Signals
  //   Output Area
endmodule

module Timer (
  input  [3:0] Time,
  input  reset,
  input  clock,
  output finish
);

  wire [3:0] counter_1_q;

  Counter #(.width(4), .max('hf)) counter_1 (
    .count(1'b1), .Q(counter_1_q), .clk(clock), .clr(reset));  // open: load, D, carry
  Comparator #(.width(4)) comparator_1 (.a(Time), .b(counter_1_q), .eq(finish));  // open: gt, lt

  // Other names for the same wires on the sheet: clk = clock; rst = reset

  // Notes on the sheet:
  //   Inputs
  //   Output
endmodule

// Data \n Path
module Data_Path_2 (
  input  [31:0] Instruction,
  input  [6:0] Keyboard,
  input  Clock,
  input  Reset,
  input  E_PC,
  input  Read_RAM,
  input  E_inst,
  input  KBD_AVAIL,
  input  PC_Address,
  output [31:0] Dir_Address,
  output halt,
  output kbd,
  output tty,
  output [31:0] RAM__w,
  output Read_RAM_2,
  output Write_RAM,
  output [6:0] tty_DATA
);

  wire add, addi, \and , and_1_out, and_2_out, andi, beq, bgtz, blez, bltz, bne, div, divu, E_HL, j, jr, lw,
       mfhi, mflo, mult, mulu, Neg, nop, \nor , \or , or_1_out, or_2_out, or_3_out, or_4_out, or_5_out,
       or_6_out, or_7_out, or_12_out, ori, pop, push, R_W, rnd, slt, slti, sltiu, sltu, sub, sw, tty_t,
       Type_I, \xor , xori, Zero;
  wire [3:0] ALU_Selector;
  wire [4:0] multiplexer_2_out, Rd, Rs, Rt;
  wire [15:0] cte;
  wire [25:0] Jump;
  wire [31:0] ALU_Output, B_C, bit_extender_2_out, cte_I15, Hi, High, Lo, multiplexer_3_out,
       multiplexer_4_out, PC, register_1_q, register_file_input_1_rf_input, Rt_t, SP;
  wire [31:7] Rs_t;

  Program_Counter program_counter_1 (
    .Branch_Control(B_C), .Instruction(PC), .Enabled(E_PC), .Clock(Clock), .Reset(Reset));
  or or_1 (or_1_out, add, sub, \and , \or );
  or or_2 (or_2_out, \nor , \xor , slt, sltu);
  or or_3 (or_3_out, mfhi, mflo, addi, andi);
  or or_4 (or_4_out, slti, ori, xori, sltiu);
  or or_5 (or_5_out, rnd, kbd, E_HL);
  or or_6 (or_6_out, or_1_out, or_2_out, or_3_out, or_4_out, or_5_out);
  and and_1 (and_1_out, E_PC, or_6_out);
  or or_7 (or_7_out, lw, pop);
  and and_2 (and_2_out, or_7_out, Read_RAM);
  or or_8 (R_W, and_1_out, and_2_out);
  Branch_Control branch_control_1 (
    .beq(beq), .PC(PC), .bne(bne), .blez(blez), .cte(cte), .bgtz(bgtz), .bltz(bltz), .Jump(Jump), .j(j),
    .jr(jr), .Rs({Rs_t, tty_DATA}), .Rt(Rt_t), .Next_Instruction(B_C));
  and and_3 (tty, tty_t, E_PC);
  or or_9 (E_HL, mult, mulu, div, divu);
  Register #(.width(32)) register_1 (.D(Instruction), .en(E_inst), .Q(register_1_q), .clk(Clock), .clr(Reset));
  Instruction_Decoder instruction_decoder_1 (
    .Instruction(register_1_q), .\nor (\nor ), .pop(pop), .push(push), .halt(halt), .rnd(rnd), .addi(addi),
    .beq(beq), .j(j), .\xor (\xor ), .tty(tty_t), .kbd(kbd), .andi(andi), .bne(bne), .slt(slt), .ori(ori),
    .blez(blez), .sltu(sltu), .xori(xori), .bgtz(bgtz), .mfhi(mfhi), .slti(slti), .bltz(bltz), .mflo(mflo),
    .sltiu(sltiu), .lw(lw), .nop(nop), .sw(sw), .jr(jr), .jump(Jump), .cte(cte), .Rs(Rs), .Rt(Rt), .Rd(Rd),
    .Tyoe_I(Type_I), .add(add), .sub(sub), .mult(mult), .mulu(mulu), .div(div), .divu(divu), .\and (\and ),
    .\or (\or ));
  or or_10 (Write_RAM, sw, push);
  Multiplexer #(.width(32), .enable("false")) multiplexer_1 (
    .in0({Rs_t, tty_DATA}), .in1(Rt_t), .out(RAM__w), .sel(sw));
  or or_11 (Read_RAM_2, lw, pop);
  Register_File_Input register_file_input_1 (
    .rnd(rnd), .RAM(Instruction), .kbd(kbd), .mfhi(mfhi), .ALU_Output(ALU_Output), .mflo(mflo), .pop(pop),
    .Keyboard(Keyboard), .lw(lw), .High(Hi), .Low(Lo), .RF_Input(register_file_input_1_rf_input),
    .KBD_AVAIL(KBD_AVAIL), .Clock(Clock));
  Multiplexer #(.width(5), .enable("false")) multiplexer_2 (.in0(Rd), .in1(Rt), .out(multiplexer_2_out), .sel(Type_I));
  RegisterFile registerfile_1 (
    .Data_Address(multiplexer_2_out), .Data_In(register_file_input_1_rf_input), .R_W(R_W), .Sel_A(Rs),
    .Sel_B(Rt), .Clock(Clock), .Reset(Reset), .Output_A({Rs_t, tty_DATA}), .Output_B(Rt_t), .High_2(Hi),
    .High(High), .E_HL(E_HL), .Low(Lo), .SP(SP), .push(push), .pop(pop), .E_PC(E_PC));
  ALU_Encoder alu_encoder_1 (
    .add(add), .\and (\and ), .mult(mult), .addi(addi), .andi(andi), .mulu(mulu), .sub(sub), .\or (\or ),
    .ori(ori), .div(div), .slt(slt), .slti(slti), .\nor (\nor ), .divu(divu), .sltu(sltu), .\xor (\xor ),
    .sltui(sltiu), .xori(xori), .ALU_Selector(ALU_Selector));
  assign cte_I15 = {{16{cte[15]}}, cte};  // Bit_Extender bit_extender_1
  Multiplexer #(.width(32), .enable("false")) multiplexer_3 (
    .in0(cte_I15), .in1(bit_extender_2_out), .out(multiplexer_3_out), .sel(or_12_out));
  or or_12 (or_12_out, andi, ori, xori);
  assign bit_extender_2_out = {{16{1'b0}}, cte};  // Bit_Extender bit_extender_2
  Multiplexer #(.width(32), .enable("false")) multiplexer_4 (
    .in0(Rt_t), .in1(multiplexer_3_out), .out(multiplexer_4_out), .sel(Type_I));
  ALU alu_1 (
    .Data_A({Rs_t, tty_DATA}), .Data_B(multiplexer_4_out), .Selector(ALU_Selector), .ALU_Output(ALU_Output),
    .Zero_Flag(Zero), .Negative_Flag(Neg), .Clock(Clock), .High(High));
  RAM_address ram_address_1 (
    .ALU(ALU_Output), .SP(SP), .sw(sw), .Dir_RAM(Dir_Address), .lw(lw), .pop(pop), .push(push), .PC(PC),
    .PC_Address(PC_Address));

  // Other names for the same wires on the sheet: Clk = Clock; Read__RAM = Read_RAM_2; Rs_t[6:0] = tty_DATA;
  //   Rst = Reset

  // Notes on the sheet:
  //   Input Area
  //   READ/WRITE ENABLER
  //   INSTRUCTION FETCH
  //   Output Area
  //   HI/LOW ENABLER
  //   READ RAM AND WRITE RAM CONTROL SIGNALS
  //   AMALIA ESTO ES TUYO
  //   INSTRUCTION DECODE AND REGISTER FETCH
  //   EXECUTION
  //   MEMORY ACCESS
endmodule

// Instruction \nDecoder
module Instruction_Decoder (
  input  [31:0] Instruction,
  output [25:0] jump,
  output [15:0] cte,
  output [4:0] Rs,
  output add,
  output \nor ,
  output pop,
  output push,
  output halt,
  output rnd,
  output addi,
  output beq,
  output j,
  output [4:0] Rt,
  output sub,
  output \xor ,
  output tty,
  output kbd,
  output andi,
  output bne,
  output [4:0] Rd,
  output mult,
  output slt,
  output ori,
  output blez,
  output mulu,
  output sltu,
  output xori,
  output bgtz,
  output Tyoe_I,
  output div,
  output mfhi,
  output slti,
  output bltz,
  output divu,
  output mflo,
  output sltiu,
  output lw,
  output \and ,
  output nop,
  output sw,
  output \or ,
  output jr
);

  wire _00_0000, _11_1000, _11_1111, comparator_2_eq, comparator_3_eq, comparator_4_eq, comparator_5_eq,
       comparator_6_eq, comparator_7_eq, comparator_10_eq, comparator_11_eq, comparator_12_eq,
       comparator_13_eq, comparator_18_eq, comparator_19_eq, comparator_22_eq, comparator_23_eq,
       comparator_24_eq, comparator_26_eq, comparator_34_eq, comparator_35_eq, comparator_36_eq,
       comparator_37_eq, comparator_38_eq, comparator_39_eq, or_1_out, or_2_out, or_3_out;

  Comparator #(.width(6)) comparator_1 (.a(Instruction[31:26]), .b({6{1'b0}}), .eq(_00_0000));  // open: gt, lt
  Comparator #(.width(6)) comparator_2 (.a(Instruction[5:0]), .b(6'b100000), .eq(comparator_2_eq));  // open: gt, lt
  Comparator #(.width(6)) comparator_3 (.a(Instruction[5:0]), .b(6'b100010), .eq(comparator_3_eq));  // open: gt, lt
  Comparator #(.width(6)) comparator_4 (.a(Instruction[5:0]), .b(6'b011000), .eq(comparator_4_eq));  // open: gt, lt
  Comparator #(.width(6)) comparator_5 (.a(Instruction[5:0]), .b(6'b011001), .eq(comparator_5_eq));  // open: gt, lt
  Comparator #(.width(6)) comparator_6 (.a(Instruction[5:0]), .b(6'b011010), .eq(comparator_6_eq));  // open: gt, lt
  Comparator #(.width(6)) comparator_7 (.a(Instruction[5:0]), .b(6'b011011), .eq(comparator_7_eq));  // open: gt, lt
  Comparator #(.width(6)) comparator_8 (.a(Instruction[31:26]), .b(6'b001000), .eq(addi));  // open: gt, lt
  and and_1 (add, _00_0000, comparator_2_eq);
  and and_2 (sub, _00_0000, comparator_3_eq);
  and and_3 (mult, _00_0000, comparator_4_eq);
  and and_4 (mulu, _00_0000, comparator_5_eq);
  and and_5 (div, _00_0000, comparator_6_eq);
  and and_6 (divu, _00_0000, comparator_7_eq);
  Comparator #(.width(6)) comparator_9 (.a(Instruction[31:26]), .b(6'b111000), .eq(_11_1000));  // open: gt, lt
  Comparator #(.width(6)) comparator_10 (.a(Instruction[5:0]), .b(6'b100100), .eq(comparator_10_eq));  // open: gt, lt
  Comparator #(.width(6)) comparator_11 (.a(Instruction[5:0]), .b(6'b100101), .eq(comparator_11_eq));  // open: gt, lt
  Comparator #(.width(6)) comparator_12 (.a(Instruction[5:0]), .b(6'b100111), .eq(comparator_12_eq));  // open: gt, lt
  Comparator #(.width(6)) comparator_13 (.a(Instruction[5:0]), .b(6'b101000), .eq(comparator_13_eq));  // open: gt, lt
  Comparator #(.width(6)) comparator_14 (.a(Instruction[31:26]), .b(6'b001100), .eq(andi));  // open: gt, lt
  Comparator #(.width(6)) comparator_15 (.a(Instruction[31:26]), .b(6'b001101), .eq(ori));  // open: gt, lt
  Comparator #(.width(6)) comparator_16 (.a(Instruction[31:26]), .b(6'b001110), .eq(xori));  // open: gt, lt
  Comparator #(.width(6)) comparator_17 (.a(Instruction[31:26]), .b({6{1'b1}}), .eq(_11_1111));  // open: gt, lt
  and and_7 (\and , _00_0000, comparator_10_eq);
  and and_8 (\or , _00_0000, comparator_11_eq);
  and and_9 (\nor , _00_0000, comparator_12_eq);
  and and_10 (\xor , _00_0000, comparator_13_eq);
  Comparator #(.width(6)) comparator_18 (.a(Instruction[5:0]), .b(6'b101010), .eq(comparator_18_eq));  // open: gt, lt
  Comparator #(.width(6)) comparator_19 (.a(Instruction[5:0]), .b(6'b101011), .eq(comparator_19_eq));  // open: gt, lt
  Comparator #(.width(6)) comparator_20 (.a(Instruction[31:26]), .b(6'b001010), .eq(slti));  // open: gt, lt
  Comparator #(.width(6)) comparator_21 (.a(Instruction[31:26]), .b(6'b001011), .eq(sltiu));  // open: gt, lt
  and and_11 (slt, _00_0000, comparator_18_eq);
  and and_12 (sltu, _00_0000, comparator_19_eq);
  or or_1 (or_1_out, addi, andi, ori, xori, slti);
  or or_2 (or_2_out, sltiu, beq, bne);
  or or_3 (or_3_out, blez, bgtz, bltz, lw, sw);
  Comparator #(.width(6)) comparator_22 (.a(Instruction[5:0]), .b(6'b010000), .eq(comparator_22_eq));  // open: gt, lt
  Comparator #(.width(6)) comparator_23 (.a(Instruction[5:0]), .b(6'b010010), .eq(comparator_23_eq));  // open: gt, lt
  or or_4 (Tyoe_I, or_1_out, or_2_out, or_3_out);
  and and_13 (mfhi, _00_0000, comparator_22_eq);
  and and_14 (mflo, _00_0000, comparator_23_eq);
  Comparator #(.width(6)) comparator_24 (.a(Instruction[5:0]), .b({6{1'b0}}), .eq(comparator_24_eq));  // open: gt, lt
  Comparator #(.width(6)) comparator_25 (.a(Instruction[31:26]), .b(6'b000010), .eq(j));  // open: gt, lt
  Comparator #(.width(6)) comparator_26 (.a(Instruction[5:0]), .b(6'b001000), .eq(comparator_26_eq));  // open: gt, lt
  Comparator #(.width(6)) comparator_27 (.a(Instruction[31:26]), .b(6'b000100), .eq(beq));  // open: gt, lt
  Comparator #(.width(6)) comparator_28 (.a(Instruction[31:26]), .b(6'b000101), .eq(bne));  // open: gt, lt
  Comparator #(.width(6)) comparator_29 (.a(Instruction[31:26]), .b(6'b000110), .eq(blez));  // open: gt, lt
  Comparator #(.width(6)) comparator_30 (.a(Instruction[31:26]), .b(6'b000111), .eq(bgtz));  // open: gt, lt
  Comparator #(.width(6)) comparator_31 (.a(Instruction[31:26]), .b(6'b000001), .eq(bltz));  // open: gt, lt
  and and_15 (nop, _00_0000, comparator_24_eq);
  and and_16 (jr, _00_0000, comparator_26_eq);
  Comparator #(.width(6)) comparator_32 (.a(Instruction[31:26]), .b(6'b100011), .eq(lw));  // open: gt, lt
  Comparator #(.width(6)) comparator_33 (.a(Instruction[31:26]), .b(6'b101011), .eq(sw));  // open: gt, lt
  Comparator #(.width(6)) comparator_34 (.a(Instruction[5:0]), .b({6{1'b0}}), .eq(comparator_34_eq));  // open: gt, lt
  Comparator #(.width(6)) comparator_35 (.a(Instruction[5:0]), .b(6'b000001), .eq(comparator_35_eq));  // open: gt, lt
  and and_17 (pop, _11_1000, comparator_34_eq);
  and and_18 (push, _11_1000, comparator_35_eq);
  Comparator #(.width(6)) comparator_36 (.a(Instruction[5:0]), .b({6{1'b1}}), .eq(comparator_36_eq));  // open: gt, lt
  Comparator #(.width(6)) comparator_37 (.a(Instruction[5:0]), .b(6'b000001), .eq(comparator_37_eq));  // open: gt, lt
  Comparator #(.width(6)) comparator_38 (.a(Instruction[5:0]), .b(6'b000010), .eq(comparator_38_eq));  // open: gt, lt
  Comparator #(.width(6)) comparator_39 (.a(Instruction[5:0]), .b(6'b000100), .eq(comparator_39_eq));  // open: gt, lt
  and and_19 (halt, _11_1111, comparator_36_eq);
  and and_20 (tty, _11_1111, comparator_37_eq);
  and and_21 (rnd, _11_1111, comparator_38_eq);
  and and_22 (kbd, _11_1111, comparator_39_eq);

  assign cte = Instruction[15:0];
  assign jump = Instruction[25:0];
  assign Rd = Instruction[15:11];
  assign Rs = Instruction[25:21];
  assign Rt = Instruction[20:16];

  // Other names for the same wires on the sheet: FUNC_CODE[5:0] = Instruction[5:0]; OP_CODE[5:0] = Instruction[31:26]

  // Notes on the sheet:
  //   op. code: 00 0000
  //   Arithmetic Instructions
  //   Type R 
  //   op. code: 11 1000
  //   op. code: 11 1111
  //   Logical Instructions
  //   Type I
  //   --------
  //   Type J
  //   --------
  //   Comparison Instructions
  //   Register Handling
  //   Jump Instructions
  //   Memory Instructions
  //   Special Instructions
endmodule

// RF \n Input
module Register_File_Input (
  input  rnd,
  input  [31:0] RAM,
  input  kbd,
  input  mfhi,
  input  [31:0] ALU_Output,
  input  mflo,
  input  pop,
  input  [6:0] Keyboard,
  input  lw,
  input  Clock,
  input  [31:0] High,
  input  KBD_AVAIL,
  input  [31:0] Low,
  output [31:0] RF_Input
);

  wire ram_t;
  wire [2:0] selector;
  wire [31:0] KBD_in, random;

  Random #(.width(32)) u_Rnd (.clk(Clock), .next(rnd), .out(random));  // open: clr
  or or_1 (ram_t, pop, lw);
  or or_2 (selector[0], kbd, ram_t, mflo);
  or or_3 (selector[1], rnd, ram_t);
  or or_4 (selector[2], mfhi, mflo);
  Multiplexer #(.width(32), .enable("false")) multiplexer_1 (
    .in0({32{1'b1}}), .in1({{25{1'b0}}, Keyboard}), .out(KBD_in), .sel(KBD_AVAIL));
  Multiplexer #(.select(3), .width(32), .enable("false")) multiplexer_2 (
    .in0(ALU_Output), .in1(KBD_in), .in2(random), .in3(RAM), .in4(High), .in5(Low), .out(RF_Input),
    .sel(selector));  // open: in6, in7

  // Other names for the same wires on the sheet: ALU[31:0] = ALU_Output; clk = Clock; KBD_t[6:0] = Keyboard
endmodule

// Register \nFile
module RegisterFile (
  input  [4:0] Data_Address,
  input  [31:0] Data_In,
  input  [31:0] High,
  input  R_W,
  input  [4:0] Sel_A,
  input  [4:0] Sel_B,
  input  Clock,
  input  Reset,
  input  E_HL,
  input  push,
  input  pop,
  input  E_PC,
  output [31:0] Output_A,
  output [31:0] Output_B,
  output [31:0] High_2,
  output [31:0] Low,
  output [31:0] SP
);

  wire and_1_out, E01, E02, E03, E04, E05, E06, E07, E08, E09, E10, E11, E12, E13, E14, E15, E16, E17, E18,
       E19, E20, E21, E22, E23, E24, E25, E26, E27, E28, E29, E30, E31, E_SP, or_1_out;
  wire [31:0] multiplexer_1_out, Out00, Out01, Out02, Out03, Out04, Out05, Out06, Out07, Out08, Out09, Out10,
       Out11, Out12, Out13, Out14, Out15, Out16, Out17, Out18, Out19, Out20, Out21, Out22, Out23, Out24,
       Out25, Out26, Out27, Out28, Out29, Out30, SP____4, SP____4_t, SP_input;

  Demultiplexer #(.select(5), .enable("false")) demultiplexer_1 (
    .out1(E01), .out2(E02), .out3(E03), .out4(E04), .out5(E05), .out6(E06), .out7(E07), .out8(E08),
    .out9(E09), .out10(E10), .out11(E11), .out12(E12), .out13(E13), .out14(E14), .out15(E15), .out16(E16),
    .out17(E17), .out18(E18), .out19(E19), .out20(E20), .out21(E21), .out22(E22), .out23(E23), .out24(E24),
    .out25(E25), .out26(E26), .out27(E27), .out28(E28), .out29(E29), .out30(E30), .out31(E31), .in(R_W),
    .sel(Data_Address));  // open: out0
  Register #(.width(32)) R00 (.D({32{1'b0}}), .Q(Out00), .clk(Clock), .clr(Reset));  // open: en
  Register #(.width(32)) R04 (.D(Data_In), .en(E04), .Q(Out04), .clk(Clock), .clr(Reset));
  Register #(.width(32)) R08 (.D(Data_In), .en(E08), .Q(Out08), .clk(Clock), .clr(Reset));
  Register #(.width(32)) R12 (.D(Data_In), .en(E12), .Q(Out12), .clk(Clock), .clr(Reset));
  Register #(.width(32)) R16 (.D(Data_In), .en(E16), .Q(Out16), .clk(Clock), .clr(Reset));
  Register #(.width(32)) R20 (.D(Data_In), .en(E20), .Q(Out20), .clk(Clock), .clr(Reset));
  Register #(.width(32)) R24 (.D(Data_In), .en(E24), .Q(Out24), .clk(Clock), .clr(Reset));
  Register #(.width(32)) R28 (.D(Data_In), .en(E28), .Q(Out28), .clk(Clock), .clr(Reset));
  Register #(.width(32)) R01 (.D(Data_In), .en(E01), .Q(Out01), .clk(Clock), .clr(Reset));
  Register #(.width(32)) R05 (.D(Data_In), .en(E05), .Q(Out05), .clk(Clock), .clr(Reset));
  Register #(.width(32)) R09 (.D(Data_In), .en(E09), .Q(Out09), .clk(Clock), .clr(Reset));
  Register #(.width(32)) R13 (.D(Data_In), .en(E13), .Q(Out13), .clk(Clock), .clr(Reset));
  Register #(.width(32)) R17 (.D(Data_In), .en(E17), .Q(Out17), .clk(Clock), .clr(Reset));
  Register #(.width(32)) R21 (.D(Data_In), .en(E21), .Q(Out21), .clk(Clock), .clr(Reset));
  Register #(.width(32)) R25 (.D(Data_In), .en(E25), .Q(Out25), .clk(Clock), .clr(Reset));
  Register #(.width(32)) R29 (.D(Data_In), .en(E29), .Q(Out29), .clk(Clock), .clr(Reset));
  Register #(.width(32)) R02 (.D(Data_In), .en(E02), .Q(Out02), .clk(Clock), .clr(Reset));
  Register #(.width(32)) R06 (.D(Data_In), .en(E06), .Q(Out06), .clk(Clock), .clr(Reset));
  Register #(.width(32)) R10 (.D(Data_In), .en(E10), .Q(Out10), .clk(Clock), .clr(Reset));
  Register #(.width(32)) R14 (.D(Data_In), .en(E14), .Q(Out14), .clk(Clock), .clr(Reset));
  Register #(.width(32)) R18 (.D(Data_In), .en(E18), .Q(Out18), .clk(Clock), .clr(Reset));
  Register #(.width(32)) R22 (.D(Data_In), .en(E22), .Q(Out22), .clk(Clock), .clr(Reset));
  Register #(.width(32)) R26 (.D(Data_In), .en(E26), .Q(Out26), .clk(Clock), .clr(Reset));
  Register #(.width(32)) R30 (.D(Data_In), .en(E30), .Q(Out30), .clk(Clock), .clr(Reset));
  Register #(.width(32)) u_High (.D(High), .en(E_HL), .Q(High_2), .clk(Clock), .clr(Reset));
  Adder #(.width(32)) adder_1 (.a(SP), .b(32'h4), .out(SP____4));  // open: cin, cout
  Multiplexer #(.width(32), .enable("false")) multiplexer_1 (
    .in0(SP____4_t), .in1(SP____4), .out(multiplexer_1_out), .sel(pop));
  Register #(.width(32)) R03 (.D(Data_In), .en(E03), .Q(Out03), .clk(Clock), .clr(Reset));
  Register #(.width(32)) R07 (.D(Data_In), .en(E07), .Q(Out07), .clk(Clock), .clr(Reset));
  Register #(.width(32)) R11 (.D(Data_In), .en(E11), .Q(Out11), .clk(Clock), .clr(Reset));
  Register #(.width(32)) R15 (.D(Data_In), .en(E15), .Q(Out15), .clk(Clock), .clr(Reset));
  Register #(.width(32)) R19 (.D(Data_In), .en(E19), .Q(Out19), .clk(Clock), .clr(Reset));
  Register #(.width(32)) R23 (.D(Data_In), .en(E23), .Q(Out23), .clk(Clock), .clr(Reset));
  Register #(.width(32)) R27 (.D(Data_In), .en(E27), .Q(Out27), .clk(Clock), .clr(Reset));
  Register #(.width(32)) u_Low (.D(Data_In), .en(E_HL), .Q(Low), .clk(Clock), .clr(Reset));
  Multiplexer #(.width(32), .enable("false")) multiplexer_2 (
    .in0(multiplexer_1_out), .in1(Data_In), .out(SP_input), .sel(E31));
  or or_1 (or_1_out, push, pop);
  and and_1 (and_1_out, or_1_out, E_PC);
  Subtractor #(.width(32)) subtractor_1 (.a(SP), .b(32'h4), .out(SP____4_t));  // open: bin, bout
  Register #(.width(32)) u_SP (.D(SP_input), .en(E_SP), .Q(SP), .clk(Clock), .clr(Reset));
  or or_2 (E_SP, Reset, and_1_out, E31);
  Multiplexer #(.select(5), .width(32), .enable("false")) multiplexer_3 (
    .in0(Out00), .in1(Out01), .in2(Out02), .in3(Out03), .in4(Out04), .in5(Out05), .in6(Out06), .in7(Out07),
    .in8(Out08), .in9(Out09), .in10(Out10), .in11(Out11), .in12(Out12), .in13(Out13), .in14(Out14),
    .in15(Out15), .in16(Out16), .in17(Out17), .in18(Out18), .in19(Out19), .in20(Out20), .in21(Out21),
    .in22(Out22), .in23(Out23), .in24(Out24), .in25(Out25), .in26(Out26), .in27(Out27), .in28(Out28),
    .in29(Out29), .in30(Out30), .in31(SP), .out(Output_A), .sel(Sel_A));
  Multiplexer #(.select(5), .width(32), .enable("false")) multiplexer_4 (
    .in0(Out00), .in1(Out01), .in2(Out02), .in3(Out03), .in4(Out04), .in5(Out05), .in6(Out06), .in7(Out07),
    .in8(Out08), .in9(Out09), .in10(Out10), .in11(Out11), .in12(Out12), .in13(Out13), .in14(Out14),
    .in15(Out15), .in16(Out16), .in17(Out17), .in18(Out18), .in19(Out19), .in20(Out20), .in21(Out21),
    .in22(Out22), .in23(Out23), .in24(Out24), .in25(Out25), .in26(Out26), .in27(Out27), .in28(Out28),
    .in29(Out29), .in30(Out30), .in31(SP), .out(Output_B), .sel(Sel_B));

  // Other names for the same wires on the sheet: Clk = Clock; DataAddress[4:0] = Data_Address; DataIn[31:0] = Data_In;
  //   High_Input[31:0] = High; High_t[31:0] = High_2; Rst = Reset; SelectA[4:0] = Sel_A; SelectB[4:0] = Sel_B

  // Notes on the sheet:
  //   Inputs
  //   Outputs
endmodule

// ALU \nEncoder
module ALU_Encoder (
  input  add,
  input  \and ,
  input  mult,
  input  addi,
  input  andi,
  input  mulu,
  input  sub,
  input  \or ,
  input  ori,
  input  div,
  input  slt,
  input  slti,
  input  \nor ,
  input  divu,
  input  sltu,
  input  \xor ,
  input  sltui,
  input  xori,
  output [3:0] ALU_Selector
);

  wire add_t, and_t, or_t, slt_t, sltu_t, xor_t;

  or or_1 (add_t, add, addi);
  or or_2 (slt_t, slt, slti);
  or or_3 (sltu_t, sltu, sltui);
  or or_4 (ALU_Selector[0], sub, sltu_t, xor_t, or_t, mulu);
  or or_5 (ALU_Selector[1], slt_t, sltu_t, \nor , xor_t, div);
  or or_6 (and_t, \and , andi);
  or or_7 (or_t, \or , ori);
  or or_8 (xor_t, \xor , xori);
  or or_9 (ALU_Selector[2], and_t, or_t, \nor , xor_t, divu);
  or or_10 (ALU_Selector[3], mult, mulu, div, divu);

  // Other names for the same wires on the sheet: _0 = ALU_Selector[0]; _1 = ALU_Selector[1]; _2 = ALU_Selector[2];
  //   _3 = ALU_Selector[3]; sltiu = sltui

  // Notes on the sheet:
  //   ALU Operations
endmodule

module ALU (
  input  [31:0] Data_A,
  input  [31:0] Data_B,
  input  [3:0] Selector,
  input  Clock,
  output [31:0] ALU_Output,
  output [31:0] High,
  output Zero_Flag,
  output Negative_Flag
);

  wire slt_bit, sltu_bit;
  wire [1:0] MiniSelector;
  wire [31:0] Add, And, DivHigh, DivLow, DivuHigh, DivuLow, Low, MultHigh, MultLow, MuluHigh, MuluLow, Nor,
       Operations, Or, slt, sltu, Sub, Xor;

  Adder #(.width(32)) adder_1 (.a(Data_A), .b(Data_B), .out(Add));  // open: cin, cout
  Multiplier #(.width(32)) multiplier_1 (.a(Data_A), .b(Data_B), .out(MuluLow), .cout(MuluHigh));  // open: cin
  Mult mult_1 (.A(Data_A), .B(Data_B), .Low(MultLow), .High(MultHigh));
  Comparator #(.width(32)) comparator_1 (.a(Data_A), .b(Data_B), .lt(slt_bit));  // open: gt, eq
  assign slt = {{31{1'b0}}, slt_bit};  // Bit_Extender bit_extender_1
  Multiplexer #(.select(2), .width(32), .enable("false")) multiplexer_1 (
    .in0(MultHigh), .in1(DivHigh), .in2(MuluHigh), .in3(DivuHigh), .out(High), .sel(MiniSelector));
  or or_1 (MiniSelector[0], Selector[1], Selector[2]);
  or or_2 (MiniSelector[1], Selector[0], Selector[2]);
  Subtractor #(.width(32)) subtractor_1 (.a(Data_A), .b(Data_B), .out(Sub));  // open: bin, bout
  Divider #(.width(32)) divider_1 (.a(Data_A), .b(Data_B), .out(DivuLow), .rem(DivuHigh));  // open: upper
  Div div_1 (.Low(DivLow), .High(DivHigh), .B(Data_B), .A(Data_A));
  Comparator #(.width(32), .mode("unsigned")) comparator_2 (.a(Data_A), .b(Data_B), .lt(sltu_bit));  // open: gt, eq
  assign sltu = {{31{1'b0}}, sltu_bit};  // Bit_Extender bit_extender_2
  Multiplexer #(.select(2), .width(32), .enable("false")) multiplexer_2 (
    .in0(MultLow), .in1(DivLow), .in2(MuluLow), .in3(DivuLow), .out(Low), .sel(MiniSelector));
  Multiplexer #(.select(3), .width(32), .enable("false")) multiplexer_3 (
    .in0(Add), .in1(Sub), .in2(slt), .in3(sltu), .in4(And), .in5(Or), .in6(Nor), .in7(Xor), .out(Operations),
    .sel(Selector[2:0]));
  assign And = Data_A & Data_B;  // AND_Gate and_1, 32 bits wide
  assign Or = Data_A | Data_B;  // OR_Gate or_3, 32 bits wide
  Multiplexer #(.width(32), .enable("false")) multiplexer_4 (
    .in0(Operations), .in1(Low), .out(ALU_Output), .sel(Selector[3]));
  assign Nor = ~(Data_A | Data_B);  // NOR_Gate nor_1, 32 bits wide
  assign Xor = Data_A ^ Data_B;  // XOR_Gate xor_1, 32 bits wide
  Comparator #(.width(32)) comparator_3 (
    .a(ALU_Output), .b({32{1'b0}}), .eq(Zero_Flag), .lt(Negative_Flag));  // open: gt

  // Other names for the same wires on the sheet: A[31:0] = Data_A; B[31:0] = Data_B; Clk = Clock;
  //   Output[31:0] = ALU_Output; Selector_t[2:0] = Selector[2:0]; Enable = Selector[3]

  // Notes on the sheet:
  //   INPUTS
  //   ARITHMETIC
  //   LOGIC
  //   OUTPUTS
endmodule

// sig \n×
module Mult (
  input  [31:0] A,
  input  [31:0] B,
  output [31:0] Low,
  output [31:0] High
);

  wire carry_low, NegOut, selectorA, selectorB;
  wire [31:0] adder_1_out, adder_2_out, bit_negator_1_output, bit_negator_2_output, multiplexer_1_out,
       multiplexer_2_out, multiplier_1_cout, multiplier_1_out, negator_1_out, negator_2_out;

  // Probe on A
  // Probe on B
  Comparator #(.width(1), .mode("unsigned")) comparator_1 (.a(1'b1), .b(A[31]), .eq(selectorA));  // open: gt, lt
  Negator #(.width(32)) negator_1 (.in(A), .out(negator_1_out));
  Negator #(.width(32)) negator_2 (.in(B), .out(negator_2_out));
  Comparator #(.width(1)) comparator_2 (.a(B[31]), .b(1'b1), .eq(selectorB));  // open: gt, lt
  Multiplexer #(.width(32), .enable("false")) multiplexer_1 (
    .in0(A), .in1(negator_1_out), .out(multiplexer_1_out), .sel(selectorA));
  Multiplexer #(.width(32), .enable("false")) multiplexer_2 (
    .in0(B), .in1(negator_2_out), .out(multiplexer_2_out), .sel(selectorB));
  Multiplier #(.width(32)) multiplier_1 (
    .a(multiplexer_1_out), .b(multiplexer_2_out), .out(multiplier_1_out), .cout(multiplier_1_cout));  // open: cin
  xor xor_1 (NegOut, selectorA, selectorB);
  Bit_Negator bit_negator_1 (.Number(multiplier_1_out), .Output(bit_negator_1_output));
  Bit_Negator bit_negator_2 (.Number(multiplier_1_cout), .Output(bit_negator_2_output));
  Adder #(.width(32)) adder_1 (.a(bit_negator_1_output), .b(32'h1), .out(adder_1_out), .cout(carry_low));  // open: cin
  Adder #(.width(32)) adder_2 (
    .a(bit_negator_2_output), .b({32{1'b0}}), .out(adder_2_out), .cin(carry_low));  // open: cout
  // Probe on Low
  Multiplexer #(.width(32), .enable("false")) multiplexer_3 (
    .in0(multiplier_1_out), .in1(adder_1_out), .out(Low), .sel(NegOut));
  Multiplexer #(.width(32), .enable("false")) multiplexer_4 (
    .in0(multiplier_1_cout), .in1(adder_2_out), .out(High), .sel(NegOut));
  // Probe on High
endmodule

// sig \n÷
module Div (
  input  [31:0] A,
  input  [31:0] B,
  output [31:0] Low,
  output [31:0] High
);

  wire is_zero;
  wire [1:0] selector;
  wire [31:0] cte, minus_neg_division, minus_positive_division, mult_1_low, multiplexer_1_out,
       multiplexer_2_out, neg_division, negator_3_out, negator_4_out, positive_division, rest;

  // Probe on A
  // Probe on B
  Negator #(.width(32)) negator_1 (.in(positive_division), .out(minus_positive_division));
  Adder #(.width(32)) adder_1 (.a(positive_division), .b(cte), .out(neg_division));  // open: cin, cout
  Negator #(.width(32)) negator_2 (.in(neg_division), .out(minus_neg_division));
  Comparator #(.width(1), .mode("unsigned")) comparator_1 (.a(1'b1), .b(A[31]), .eq(selector[1]));  // open: gt, lt
  Negator #(.width(32)) negator_3 (.in(A), .out(negator_3_out));
  Negator #(.width(32)) negator_4 (.in(B), .out(negator_4_out));
  Comparator #(.width(1)) comparator_2 (.a(B[31]), .b(1'b1), .eq(selector[0]));  // open: gt, lt
  Comparator #(.width(32)) comparator_3 (.a(rest), .b({32{1'b0}}), .eq(is_zero));  // open: gt, lt
  Multiplexer #(.width(32), .enable("false")) multiplexer_1 (
    .in0(A), .in1(negator_3_out), .out(multiplexer_1_out), .sel(selector[1]));
  Multiplexer #(.width(32), .enable("false")) multiplexer_2 (
    .in0(B), .in1(negator_4_out), .out(multiplexer_2_out), .sel(selector[0]));
  Divider #(.width(32)) divider_1 (
    .a(multiplexer_1_out), .b(multiplexer_2_out), .out(positive_division), .rem(rest));  // open: upper
  Multiplexer #(.width(32), .enable("false")) multiplexer_3 (.in0(32'h1), .in1({32{1'b0}}), .out(cte), .sel(is_zero));
  Mult mult_1 (.A(B), .B(Low), .Low(mult_1_low));  // open: High
  Multiplexer #(.select(2), .width(32), .enable("false")) multiplexer_4 (
    .in0(positive_division), .in1(minus_positive_division), .in2(minus_neg_division), .in3(neg_division),
    .out(Low), .sel(selector));
  Subtractor #(.width(32)) subtractor_1 (.a(A), .b(mult_1_low), .out(High));  // open: bin, bout
  // Probe on Low
  // Probe on High

  // Other names for the same wires on the sheet: result[31:0] = Low; selectorB = selector[0]; selectorA = selector[1]
endmodule

// PC
module Program_Counter (
  input  [31:0] Branch_Control,
  input  Enabled,
  input  Clock,
  input  Reset,
  output [31:0] Instruction
);

  Register #(.width(32)) PC (.D(Branch_Control), .en(Enabled), .Q(Instruction), .clk(Clock), .clr(Reset));
endmodule

// Branch \nControl
module Branch_Control (
  input  beq,
  input  [31:0] PC,
  input  bne,
  input  blez,
  input  [15:0] cte,
  input  bgtz,
  input  bltz,
  input  [25:0] Jump,
  input  j,
  input  jr,
  input  [31:0] Rs,
  input  [31:0] Rt,
  output [31:0] Next_Instruction
);

  wire and_1_out, and_2_out, and_3_out, and_4_out, and_5_out, or_1_out, or_2_out, Rs____0, Rs_____0,
       Rs______Rt;
  wire [1:0] selector;
  wire [31:0] PC____4, PC____4___4___offset;
  wire [31:18] _4___offset;

  or or_1 (or_1_out, Rs_____0, Rs____0);
  and and_1 (and_1_out, beq, Rs______Rt);
  and and_2 (and_2_out, ~Rs______Rt, bne);  // AND_Gate
  and and_3 (and_3_out, blez, or_1_out);
  and and_4 (and_4_out, ~or_1_out, bgtz);  // AND_Gate
  and and_5 (and_5_out, bltz, Rs____0);
  Comparator #(.width(32)) comparator_1 (.a(Rs), .b(Rt), .eq(Rs______Rt));  // open: gt, lt
  assign _4___offset = {{13{cte[15]}}, cte[15]};  // Bit_Extender bit_extender_1
  Adder #(.width(32)) adder_1 (.a(PC), .b(32'h4), .out(PC____4));  // open: cin, cout
  Adder #(.width(32)) adder_2 (
    .a(PC____4), .b({_4___offset, cte, 2'b00}), .out(PC____4___4___offset));  // open: cin, cout
  or or_2 (or_2_out, and_1_out, and_2_out, and_3_out, and_4_out, and_5_out);
  or or_3 (selector[0], j, jr);
  or or_4 (selector[1], or_2_out, jr);
  Comparator #(.width(32)) comparator_2 (.a(Rs), .b({32{1'b0}}), .eq(Rs_____0), .lt(Rs____0));  // open: gt
  Multiplexer #(.select(2), .width(32), .enable("false")) multiplexer_1 (
    .in0(PC____4), .in1({PC[31:28], Jump, 2'b00}), .in2(PC____4___4___offset), .in3(Rs),
    .out(Next_Instruction), .sel(selector));

  // Other names for the same wires on the sheet: _4___offset[17:2] = cte; jump_destiny[31:2] = {PC[31:28], Jump}
endmodule

// -x
module Bit_Negator (
  input  [31:0] Number,
  output [31:0] Output
);

  not not_1 (Output[0], Number[0]);
  not not_2 (Output[1], Number[1]);
  not not_3 (Output[2], Number[2]);
  not not_4 (Output[3], Number[3]);
  not not_5 (Output[4], Number[4]);
  not not_6 (Output[5], Number[5]);
  not not_7 (Output[6], Number[6]);
  not not_8 (Output[7], Number[7]);
  not not_9 (Output[8], Number[8]);
  not not_10 (Output[9], Number[9]);
  not not_11 (Output[10], Number[10]);
  not not_12 (Output[11], Number[11]);
  not not_13 (Output[12], Number[12]);
  not not_14 (Output[13], Number[13]);
  not not_15 (Output[14], Number[14]);
  not not_16 (Output[15], Number[15]);
  not not_17 (Output[16], Number[16]);
  not not_18 (Output[17], Number[17]);
  not not_19 (Output[18], Number[18]);
  not not_20 (Output[19], Number[19]);
  not not_21 (Output[20], Number[20]);
  not not_22 (Output[21], Number[21]);
  not not_23 (Output[22], Number[22]);
  not not_24 (Output[23], Number[23]);
  not not_25 (Output[24], Number[24]);
  not not_26 (Output[25], Number[25]);
  not not_27 (Output[26], Number[26]);
  not not_28 (Output[27], Number[27]);
  not not_29 (Output[28], Number[28]);
  not not_30 (Output[29], Number[29]);
  not not_31 (Output[30], Number[30]);
  not not_32 (Output[31], Number[31]);
endmodule

// RAM \nread/write
module RAM_address (
  input  [31:0] ALU,
  input  [31:0] SP,
  input  [31:0] PC,
  input  sw,
  input  lw,
  input  pop,
  input  push,
  input  PC_Address,
  output [31:0] Dir_RAM
);

  wire [1:0] selector;
  wire [31:0] multiplexer_1_out, subtractor_1_out;

  Multiplexer #(.width(32), .enable("false")) multiplexer_1 (
    .in0(SP), .in1(subtractor_1_out), .out(multiplexer_1_out), .sel(push));
  Subtractor #(.width(32)) subtractor_1 (.a(SP), .b(32'h4), .out(subtractor_1_out));  // open: bin, bout
  Multiplexer #(.select(2), .width(32), .enable("false")) multiplexer_2 (
    .in0(PC), .in1(ALU), .in2(multiplexer_1_out), .in3(PC), .out(Dir_RAM), .sel(selector));
  or or_1 (selector[1], pop, PC_Address, push);
  or or_2 (selector[0], sw, PC_Address, lw);
endmodule

// READ \n RAM
module Read_RAM (
  input  [31:0] Dir_RAM,
  input  [31:0] Bank_0,
  input  [31:0] Bank_1,
  input  [31:0] Bank_2,
  input  [31:0] Bank_3,
  output [31:0] Value
);

  wire [31:0] multiplexer_1_out;

  Multiplexer #(.select(2), .width(32), .enable("false")) multiplexer_1 (
    .in0(Bank_0), .in1(Bank_1), .in2(Bank_2), .in3(Bank_3), .out(multiplexer_1_out), .sel(Dir_RAM[3:2]));
  Little_Endian little_endian_1 (.in_1(multiplexer_1_out), .out_2(Value));

  // Other names for the same wires on the sheet: selector[1:0] = Dir_RAM[3:2]
endmodule

// WRITE \n RAM
module Write_RAM (
  input  [31:0] Dir_RAM,
  input  [31:0] Value,
  output [15:0] ADDR,
  output [3:0] Mask,
  output [31:0] Bank_0,
  output [31:0] Bank_1,
  output [31:0] Bank_2,
  output [31:0] Bank_3
);

  wire [31:0] little_endian_1_out_2;

  Demultiplexer #(.select(2), .width(32), .enable("false")) demultiplexer_1 (
    .out0(Bank_0), .out1(Bank_1), .out2(Bank_2), .out3(Bank_3), .in(little_endian_1_out_2), .sel(Dir_RAM[3:2]));
  Little_Endian little_endian_1 (.in_1(Value), .out_2(little_endian_1_out_2));
  Demultiplexer #(.select(2), .enable("false")) demultiplexer_2 (
    .out0(Mask[0]), .out1(Mask[1]), .out2(Mask[2]), .out3(Mask[3]), .in(1'b1), .sel(Dir_RAM[3:2]));

  assign ADDR = Dir_RAM[19:4];

  // Other names for the same wires on the sheet: selector[1:0] = Dir_RAM[3:2]
endmodule

module Little_Endian (
  input  [31:0] in_1,
  output [31:0] out_2
);


  assign out_2 = {in_1[7:0], in_1[15:8], in_1[23:16], in_1[31:24]};

  // Notes on the sheet:
  //   Instruction
  //   Output
endmodule
